// Logisim project Mult.circ as structural Verilog
module mux4_1 (
  input  A0,
  input  A1,
  input  D0,
  input  D1,
  input  D2,
  input  D3,
  output Y
);

  wire not_1_out, not_2_out, \И_2_out , \И_3_out , \И_4_out , \И_out ;

  not not_1 (not_1_out, A0);
  not not_2 (not_2_out, A1);
  and \u_И  (\И_out , not_1_out, not_2_out, D0);
  and \u_И_2  (\И_2_out , not_2_out, A0, D1);
  and \u_И_3  (\И_3_out , not_1_out, D2, A1);
  and \u_И_4  (\И_4_out , A0, D3, A1);
  or \u_ИЛИ  (Y, \И_out , \И_2_out , \И_3_out , \И_4_out );
endmodule

module MUX16_1 (
  input  D0,
  input  D1,
  input  D2,
  input  D3,
  input  D4,
  input  D5,
  input  D6,
  input  D7,
  input  D8,
  input  D9,
  input  D10,
  input  D11,
  input  D12,
  input  D13,
  input  D14,
  input  D15,
  input  A0,
  input  A1,
  input  A2,
  input  A3,
  output out_21
);

  wire MXU_2_y, MXU_3_y, MXU_4_y, MXU_y;

  mux4_1 MXU (.A0(A0), .A1(A1), .D0(D0), .D1(D1), .D2(D2), .D3(D3), .Y(MXU_y));
  mux4_1 MXU_2 (.A0(A0), .A1(A1), .D0(D4), .D1(D5), .D2(D6), .D3(D7), .Y(MXU_2_y));
  mux4_1 MXU_3 (.A0(A0), .A1(A1), .D0(D8), .D1(D9), .D2(D10), .D3(D11), .Y(MXU_3_y));
  mux4_1 MXU_4 (.A0(A0), .A1(A1), .D0(D12), .D1(D13), .D2(D14), .D3(D15), .Y(MXU_4_y));
  mux4_1 MXU_5 (.A0(A2), .A1(A3), .D0(MXU_y), .D1(MXU_2_y), .D2(MXU_3_y), .D3(MXU_4_y), .Y(out_21));
endmodule

module DeShif (
  input  A,
  input  B,
  input  C,
  input  D,
  output a_2,
  output b_2,
  output c_2,
  output d_2,
  output e,
  output f,
  output g
);

  wire and_1_out, and_2_out, and_3_out, and_4_out, and_5_out, and_6_out, and_7_out, and_8_out, and_9_out,
       and_10_out, and_11_out, and_12_out, and_13_out, and_14_out, and_15_out, and_16_out, not_1_out,
       not_2_out, not_3_out, not_4_out, not_5_out, not_6_out, not_7_out, not_8_out, not_9_out, not_10_out,
       not_11_out, not_12_out, not_13_out, not_14_out, not_15_out, not_16_out, not_17_out, not_18_out,
       not_19_out, not_20_out, not_21_out;

  and and_1 (and_1_out, B, D);
  not not_1 (not_1_out, B);
  and and_2 (and_2_out, not_1_out, not_2_out);
  not not_2 (not_2_out, D);
  not not_3 (not_3_out, B);
  not not_4 (not_4_out, C);
  and and_3 (and_3_out, not_4_out, not_5_out);
  not not_5 (not_5_out, D);
  and and_4 (and_4_out, C, D);
  or or_1 (c_2, B, D, not_6_out);
  not not_6 (not_6_out, C);
  not not_7 (not_7_out, B);
  and and_5 (and_5_out, not_7_out, C);
  not not_8 (not_8_out, B);
  and and_6 (and_6_out, not_8_out, not_9_out);
  not not_9 (not_9_out, D);
  and and_7 (and_7_out, C, not_10_out);
  not not_10 (not_10_out, D);
  and and_8 (and_8_out, B, not_11_out, D);
  not not_11 (not_11_out, C);
  not not_12 (not_12_out, B);
  and and_9 (and_9_out, not_12_out, not_13_out);
  not not_13 (not_13_out, D);
  and and_10 (and_10_out, C, not_14_out);
  not not_14 (not_14_out, D);
  and and_11 (and_11_out, B, not_15_out);
  not not_15 (not_15_out, C);
  and and_12 (and_12_out, B, not_16_out);
  not not_16 (not_16_out, D);
  not not_17 (not_17_out, C);
  and and_13 (and_13_out, not_17_out, not_18_out);
  not not_18 (not_18_out, D);
  and and_14 (and_14_out, B, not_19_out);
  not not_19 (not_19_out, C);
  not not_20 (not_20_out, B);
  and and_15 (and_15_out, not_20_out, C);
  and and_16 (and_16_out, C, not_21_out);
  not not_21 (not_21_out, D);
  or or_2 (a_2, A, C, and_1_out, and_2_out);
  or or_3 (b_2, not_3_out, and_3_out, and_4_out);
  or or_4 (d_2, A, and_5_out, and_6_out, and_7_out, and_8_out);
  or or_5 (e, and_9_out, and_10_out);
  or or_6 (f, A, and_11_out, and_12_out, and_13_out);
  or or_7 (g, A, and_14_out, and_15_out, and_16_out);
endmodule

module DeMult (
  input  D,
  input  A0,
  input  A1,
  output Y0,
  output Y1,
  output Y2,
  output Y3
);

  wire DD_a_2, DD_b_2, DD_c_2, DD_d_2, DD_e, DD_f, DD_g, not_1_out, not_2_out, not_3_out, not_4_out;

  not not_1 (not_1_out, A1);
  not not_2 (not_2_out, A0);
  not not_3 (not_3_out, A1);
  not not_4 (not_4_out, A0);
  and and_1 (Y3, D, A1, A0);
  and and_2 (Y0, D, not_1_out, not_2_out);
  and and_3 (Y1, D, not_3_out, A0);
  and and_4 (Y2, D, A1, not_4_out);
  DeShif DD (
    .A(Y3), .B(Y2), .C(Y1), .D(Y0), .a_2(DD_a_2), .b_2(DD_b_2), .c_2(DD_c_2), .d_2(DD_d_2), .e(DD_e),
    .f(DD_f), .g(DD_g));
  _7_Segment_Display u_7_segment_display_1 (
    .g(DD_g), .f(DD_f), .a(DD_a_2), .b(DD_b_2), .e(DD_e), .d(DD_d_2), .c(DD_c_2));  // open: dp

  // Notes on the sheet:
  //   DD
endmodule
